# Fritzing sketch Neopixel_V1 (saved by Fritzing 1.0.4)

parts:
  Parça1 = Arduino Nano (Rev3.0)
  NEOPIXEL2 = Neopixel Strip -- Black (60/m) [part_number=1461]
  USBTTL1 = USB TTL Serial Cable  # not connected
  JACK1 = 2.1mm Barrel Jack with Terminal Block

nets:
  N1: Parça1.D3, NEOPIXEL2.DI
  N2: NEOPIXEL2.+5V, JACK1.POS
  N3: NEOPIXEL2.GND, JACK1.NEG

notes:
  5V Power Supply
  Pc Usb Connector
  ←
  Bu kırmızı kablo opsiyoneldir, bilgisayar ile kablo bağlantınız kesilse dahi lediniz çalışmaya devam etsin istiyorsanız eklemelisiniz.
  This red cable is optional, you should add it if you want your LED to continue working even if your cable connection to the computer is disconnected.

custom parts:
  Neopixel Strip -- Black (60/m): Neopixel Strip, Black, 60 pixels per meter.
